# Fritzing sketch doubleNeopixelBoard (saved by Fritzing 0.9.3b)
circuit board: 1cm x 1cm
breadboards: 1

parts:
  J1 = male pin header, 3 pins [form="♂ (male)"]
  J2 = male pin header, 3 pins [form="♂ (male)"]
  Part2 = ws2812b [package="smd 2812b"]
  C1 = Capacitor [package=0805]
  Part1 = ws2812b [package="smd 2812b"]

nets:
  VDD: J1.pin1, J2.pin1, Part2.VDD, C1.2, Part1.VDD
  N1: J1.pin2, Part2.DIN, Part1.DIN
  VSS: J1.pin3, J2.pin3, Part2.VSS, C1.1, Part1.VSS
  N2: J2.pin2, Part2.DOUT, Part1.DOUT

notes:
  Vin
  GND
  Di
  Do
  C1
